// Logisim project muxrisccore.circ as structural Verilog: 1 circuit, main circuit main
module main (
);

  wire clock_1_out, clock_2_out, comparator_1_eq, comparator_2_eq, multiplexer_3_out;
  wire [1:0] bitselector_1_out, multiplexer_1_out, register_1_q;
  wire [15:0] counter_1_q, multiplexer_2_out;
  wire [63:0] demultiplexer_1_out0, multiplexer_4_out, ram_1_dout;

  Register #(.trigger("falling"), .width(2)) register_1 (.Q(register_1_q));  // open: D, en, clk, clr
  Multiplexer #(.select(2), .width(2)) multiplexer_1 (
    .in0(2'b00), .out(multiplexer_1_out), .sel(register_1_q));  // open: in1, in2, in3
  Comparator #(.width(2)) comparator_1 (.a(multiplexer_1_out), .b(2'b00), .eq(comparator_1_eq));  // open: gt, lt
  Counter #(.max('hffff), .trigger("falling"), .width(16)) counter_1 (
    .load(comparator_2_eq), .D({16{1'b0}}), .count(comparator_1_eq), .Q(counter_1_q), .clk(clock_1_out));  // open: carry, up, clr
  Clock clock_1 (.out(clock_1_out));
  Multiplexer #(.select(2), .width(16)) multiplexer_2 (
    .in0(counter_1_q), .out(multiplexer_2_out), .sel(multiplexer_1_out));  // open: in1, in2, in3
  Multiplexer #(.select(2)) multiplexer_3 (
    .out(multiplexer_3_out), .sel(multiplexer_1_out));  // open: in0, in1, in2, in3
  RAM #(.addrWidth(16), .dataWidth(64), .enables("line"), .\type ("nonvolatile")) ram_1 (
    .addr(multiplexer_2_out), .we(multiplexer_3_out), .clk(clock_2_out), .din(multiplexer_4_out),
    .dout(ram_1_dout));
  Clock clock_2 (.out(clock_2_out));
  Multiplexer #(.select(2), .width(64)) multiplexer_4 (
    .out(multiplexer_4_out), .sel(multiplexer_1_out));  // open: in0, in1, in2, in3
  Demultiplexer #(.select(2), .width(64)) demultiplexer_1 (
    .out0(demultiplexer_1_out0), .in(ram_1_dout), .sel(multiplexer_1_out));  // open: out1, out2, out3
  BitSelector #(.group(2), .width(64)) bitselector_1 (
    .in(demultiplexer_1_out0), .out(bitselector_1_out), .sel({5{1'b0}}));
  Comparator #(.width(2)) comparator_2 (.a(bitselector_1_out), .b(2'b11), .eq(comparator_2_eq));  // open: gt, lt
endmodule
